# Fritzing sketch RFID - LED (saved by Fritzing 0.8.5b)
breadboards: 1

parts:
  Part1 = Arduino Uno (Rev3)
  Part2 = RFID-RC522-v2
  R1 = Resistor [tolerance=±5% resistance=220 package=THT]
  R2 = Resistor [tolerance=±5% resistance=220 package=THT]
  R3 = Resistor [tolerance=±5% resistance=220 package=THT]
  R4 = Resistor [tolerance=±5% resistance=220 package=THT]
  R5 = Resistor [tolerance=±5% resistance=220 package=THT]
  R6 = Resistor [tolerance=±5% resistance=220 package=THT]
  LED4 = LED - 5mm [color="Red (633nm)" package="5 mm [THT]"]
  LED1 = LED - 5mm [color="Red (633nm)" package="5 mm [THT]"]
  LED5 = LED - 5mm [color="Red (633nm)" package="5 mm [THT]"]
  LED6 = LED - 5mm [color="Red (633nm)" package="5 mm [THT]"]
  LED2 = LED - 5mm [color="Red (633nm)" package="5 mm [THT]"]
  LED3 = LED - 5mm [color="Red (633nm)" package="5 mm [THT]"]

nets:
  N1: Part1.D9_PWM, Part2.RST
  N2: Part1.D10_PWM/SS, Part2.SDA
  N3: Part1.D11_PWM/MOSI, Part2.MOSI
  N4: Part1.D12/MISO, Part2.MISO
  N5: Part1.D13/SCK, Part2.SCK
  N6: Part1.D2, R3.Pin_1
  N7: Part1.D3_PWM, R2.Pin_1
  N8: Part1.D4, R1.Pin_1
  N9: Part1.D5_PWM, R6.Pin_1
  N10: Part1.D6_PWM, R5.Pin_1
  N11: Part1.D7, R4.Pin_1
  3V3: Part1.3V3, Part2.3.3V
  GND: Part1.GND, Part2.GND
  N12: R1.Pin_0, LED1.anode
  N13: R2.Pin_0, LED2.anode
  N14: R3.Pin_0, LED3.anode
  N15: R4.Pin_0, LED4.anode
  N16: R5.Pin_0, LED5.anode
  N17: R6.Pin_0, LED6.anode
  N18: LED4.cathode, LED1.cathode, LED5.cathode, LED6.cathode, LED2.cathode, LED3.cathode

custom parts:
  RFID-RC522-v2: A simple China made RFID-RC522 Reader; do check the pin labels, as this is a MFRC522 based clone.
